// Digital circuit ALU.dig as structural Verilog
module ALU (
  input  [7:0] a,
  input  [7:0] b,
  input  [3:0] flags_in,
  input  [3:0] funct,
  output [7:0] s,
  output [3:0] flags_out
);

  wire adc, add, adder, \and , \or , rol, ror, sbc, shl, shr, sub, subtract, \xor , xor_2_out, xor_3_out,
       xor_4_out;
  wire [7:0] add_1_s, and_2_out, bitextender_1_out, or_3_out, shl_2_out, shl_out, shr_2_out, shr_out,
       xor_1_out, xor_5_out;

  Demultiplexer #(.Selector_Bits(4)) demultiplexer_1 (
    .sel(funct), .in(1'b1), .out_0(add), .out_1(adc), .out_2(sub), .out_3(sbc), .out_4(\and ), .out_5(\or ),
    .out_6(\xor ), .out_7(shl), .out_8(shr), .out_9(rol), .out_10(ror));  // open: out_11, out_12, out_13, out_14, out_15
  or or_1 (adder, sbc, sub, adc, add);
  or or_2 (subtract, sbc, sub);
  BitExtender #(.inputBits(1), .outputBits(8)) bitextender_1 (.in(subtract), .out(bitextender_1_out));
  assign xor_1_out = b ^ bitextender_1_out;  // XOr xor_1, 8 bits wide
  xor xor_2 (xor_2_out, subtract, flags_in[2]);
  xor xor_3 (xor_3_out, add_1_s[7], a[7]);
  and and_1 (flags_out[0], xor_3_out, xor_4_out);
  xor xor_4 (xor_4_out, xor_1_out[7], add_1_s[7]);
  Add #(.Bits(8)) add_1 (.a(a), .b(xor_1_out), .c_i(xor_2_out), .s(add_1_s), .c_o(flags_out[2]));
  assign and_2_out = a & b;  // And and_2, 8 bits wide
  assign or_3_out = a | b;  // Or or_3, 8 bits wide
  assign xor_5_out = a ^ b;  // XOr xor_5, 8 bits wide
  assign {flags_out[3], s[6:0]} = adder ? add_1_s : 8'bz;  // Driver driver_1
  assign {flags_out[3], s[6:0]} = \and  ? and_2_out : 8'bz;  // Driver driver_2
  assign {flags_out[3], s[6:0]} = \or  ? or_3_out : 8'bz;  // Driver driver_3
  assign {flags_out[3], s[6:0]} = \xor  ? xor_5_out : 8'bz;  // Driver driver_4
  assign {flags_out[3], s[6:0]} = shl ? shl_out : 8'bz;  // Driver driver_5
  assign {flags_out[3], s[6:0]} = shr ? shr_out : 8'bz;  // Driver driver_6
  assign {flags_out[3], s[6:0]} = rol ? shl_2_out : 8'bz;  // Driver driver_7
  assign {flags_out[3], s[6:0]} = ror ? shr_2_out : 8'bz;  // Driver driver_8
  nor nor_1 (flags_out[1], flags_out[3], s[6], s[5], s[4], s[3], s[2], s[1], s[0]);
  BarrelShifter #(.Bits(8)) u_shl (.in(a), .shift(4'b0001), .out(shl_out));
  BarrelShifter #(.Bits(8), .direction("right")) u_shr (.in(a), .shift(4'b0001), .out(shr_out));
  BarrelShifter #(.Bits(8), .barrelShifterMode("rotate")) shl_2 (.in(a), .shift(4'b0001), .out(shl_2_out));
  BarrelShifter #(.Bits(8), .barrelShifterMode("rotate"), .direction("right")) shr_2 (
    .in(a), .shift(4'b0001), .out(shr_2_out));

  assign s[7] = flags_out[3];

  // Other names for the same wires on the sheet: c = flags_out[2]; f_v = flags_in[0]; flags[3:0] = flags_in;
  //   f_z = flags_in[1]; f_c = flags_in[2]; f_n = flags_in[3]; n = flags_out[3]; v = flags_out[0]; z = flags_out[1]

  // Notes on the sheet:
  //   Driver Signals
  //   Adder
  //   Overflow
endmodule
