// Digital circuit CPU.dig as structural Verilog
module CPU (
  input  in_1,
  input  clk,
  output [7:0] Data_OUT,
  output [15:0] Addr_OUT
);

  wire ALU_Out_Write_Data_Bus, ALU_Write_Flag_Register, button_1_out, Clock, counterpreset_1_ovf,
       demultiplexer_1_out_0, demultiplexer_1_out_1, Immediate_Write_Data_Bus, IR0_Read_Data_Bus,
       IR1_Read_Data_Bus, IR2_Read_Data_Bus, Memory_Output_Enable, Memory_Write_Enable,
       Microcode_Step_Counter_Clear, Microcode_Step_Counter_ovf, multiplexer_1_out, nor_1_out,
       Program_Conter_Read_Address_Bus, Program_Conter_Write_Address_Bus, Program_Counter_Increase_Enable,
       RD_Read_Data_Bus, RD_write_Data_Bus, Read_Data_Bus, RS0_Write_ALU_A, RS0_Write_Data_Bus,
       RS1_Write_ALU_B, RS1_Write_Data_Bus, RS_Buffer, RS_Write_Address_Bus, Write_Data_Bus;
  wire [3:0] alu_1_p1, alu_1_p3, Instruction_Flags, Instruction_Opcode, Instruction_RS0, Instruction_RS1,
       Microcode_Step_Counter_out, multiplexer_2_out;
  wire [5:0] uCode_3_d;
  wire [7:0] alu_1_p2, alu_1_p5, alu_1_p6, driver_3_out, driver_11_out, driver_12_out, driver_13_out,
       driver_16_out, Instruction_Immediate, ramdualport_1_d, Register_File_da, Register_File_db;
  wire [7:4] uCode_2_d;
  wire [15:0] add_1_s, bitextender_1_out, counterpreset_1_out, driver_1_out, rs1_buf_q;

  Counter #(.Bits(4)) Microcode_Step_Counter (
    .en(1'b1), .C(Clock), .clr(Microcode_Step_Counter_Clear), .out(Microcode_Step_Counter_out),
    .ovf(Microcode_Step_Counter_ovf));
  LED led_1 (.in(Microcode_Step_Counter_ovf));
  EEPROM #(.AddrBits(8), .Bits(8)) uCode_3 (
    .A({Instruction_Opcode, Microcode_Step_Counter_out}), .CS(1'b1), .WE(1'b0), .OE(1'b1),
    .D({Memory_Output_Enable, Memory_Write_Enable, uCode_3_d}));
  EEPROM #(.AddrBits(8), .Bits(8)) uCode_2 (
    .A({Instruction_Opcode, Microcode_Step_Counter_out}), .CS(1'b1), .WE(1'b0), .OE(1'b1),
    .D({uCode_2_d, ALU_Write_Flag_Register, ALU_Out_Write_Data_Bus, RS1_Write_ALU_B, RS0_Write_ALU_A}));
  assign driver_1_out = Program_Conter_Read_Address_Bus ? Addr_OUT : 16'bz;  // Driver driver_1
  CounterPreset #(.Bits(16)) counterpreset_1 (
    .en(Program_Counter_Increase_Enable), .C(Clock), .dir(1'b0), .in(driver_1_out),
    .ld(Program_Conter_Read_Address_Bus), .clr(1'b0), .out(counterpreset_1_out), .ovf(counterpreset_1_ovf));
  LED led_2 (.in(counterpreset_1_ovf));
  assign Addr_OUT = Program_Conter_Write_Address_Bus ? counterpreset_1_out : 16'bz;  // Driver driver_2
  EEPROM #(.AddrBits(8), .Bits(8)) uCode_1 (
    .A({Instruction_Opcode, Microcode_Step_Counter_out}), .CS(1'b1), .WE(1'b0), .OE(1'b1),
    .D({Read_Data_Bus, Write_Data_Bus, Immediate_Write_Data_Bus, RS_Buffer, RS_Write_Address_Bus, RS1_Write_Data_Bus, RS0_Write_Data_Bus, RD_Read_Data_Bus}));
  RAMDualPort #(.AddrBits(15), .Bits(8)) ramdualport_1 (
    .A(Addr_OUT[14:0]), .Din(Data_OUT), .str(Memory_Write_Enable), .C(Clock), .ld(demultiplexer_1_out_1),
    .D(ramdualport_1_d));
  EEPROM #(.AddrBits(15), .Bits(8)) eeprom_1 (
    .A(Addr_OUT[14:0]), .CS(1'b1), .WE(1'b0), .OE(demultiplexer_1_out_0), .D(ramdualport_1_d));
  EEPROM #(.AddrBits(8), .Bits(8)) uCode_0 (
    .A({Instruction_Opcode, Microcode_Step_Counter_out}), .CS(1'b1), .WE(1'b0), .OE(1'b1),
    .D({RD_write_Data_Bus, IR2_Read_Data_Bus, IR1_Read_Data_Bus, IR0_Read_Data_Bus, Program_Conter_Read_Address_Bus, Program_Conter_Write_Address_Bus, Program_Counter_Increase_Enable, Microcode_Step_Counter_Clear}));
  Demultiplexer demultiplexer_1 (
    .sel(Addr_OUT[15]), .in(Memory_Output_Enable), .out_0(demultiplexer_1_out_0),
    .out_1(demultiplexer_1_out_1));
  assign driver_3_out = Read_Data_Bus ? ramdualport_1_d : 8'bz;  // Driver driver_3
  assign Addr_OUT = RS_Write_Address_Bus ? add_1_s : 16'bz;  // Driver driver_4
  assign driver_3_out = ALU_Out_Write_Data_Bus ? alu_1_p2 : 8'bz;  // Driver driver_5
  assign Data_OUT = Write_Data_Bus ? driver_3_out : 8'bz;  // Driver driver_6
  assign driver_3_out = RD_write_Data_Bus ? Register_File_db : 8'bz;  // Driver driver_7
  assign driver_3_out = RS1_Write_Data_Bus ? Register_File_db : 8'bz;  // Driver driver_8
  assign driver_3_out = RS0_Write_Data_Bus ? Register_File_da : 8'bz;  // Driver driver_9
  assign driver_3_out = Immediate_Write_Data_Bus ? Instruction_Immediate : 8'bz;  // Driver driver_10
  nor nor_1 (nor_1_out, Instruction_Flags[0], Instruction_Flags[1], Instruction_Flags[2], Instruction_Flags[3]);
  Add #(.Bits(16)) add_1 (.a(bitextender_1_out), .b(rs1_buf_q), .c_i(1'b0), .s(add_1_s));  // open: c_o
  Clock clock_1 (.CLK(clk), .MODE(in_1), .STEP(button_1_out), .SIGNAL(Clock));
  Button button_1 (.out(button_1_out));
  Multiplexer multiplexer_1 (.sel(nor_1_out), .in_0(RD_Read_Data_Bus), .in_1(1'b0), .out(multiplexer_1_out));
  BitExtender bitextender_1 (.in(Instruction_Immediate), .out(bitextender_1_out));
  // ALU alu_1: pin names not known; wires that end beside it: alu_1_p1, alu_1_p2, alu_1_p3, Instruction_Immediate[3:0], alu_1_p5, alu_1_p6
  Register #(.Bits(4)) register_1 (.D(alu_1_p1), .C(Clock), .en(ALU_Write_Flag_Register), .Q(alu_1_p3));
  Register #(.Bits(8)) IR_2 (.D(driver_11_out), .C(Clock), .en(IR2_Read_Data_Bus), .Q(Instruction_Immediate));
  assign driver_11_out = IR2_Read_Data_Bus ? driver_3_out : 8'bz;  // Driver driver_11
  Multiplexer #(.Bits(4)) multiplexer_2 (
    .sel(RD_write_Data_Bus), .in_0(Instruction_RS1), .in_1(Instruction_Flags), .out(multiplexer_2_out));
  Register #(.Bits(8)) rs0_buf (.D(Register_File_da), .C(Clock), .en(RS_Buffer), .Q(rs1_buf_q[15:8]));
  Register #(.Bits(8)) rs1_buf (.D(Register_File_db), .C(Clock), .en(RS_Buffer), .Q(rs1_buf_q[7:0]));
  Register #(.Bits(8)) IR_1 (
    .D(driver_12_out), .C(Clock), .en(IR1_Read_Data_Bus), .Q({Instruction_RS1, Instruction_RS0}));
  assign driver_12_out = IR1_Read_Data_Bus ? driver_3_out : 8'bz;  // Driver driver_12
  assign driver_13_out = RD_Read_Data_Bus ? driver_3_out : 8'bz;  // Driver driver_13
  RegisterFile #(.AddrBits(4), .Bits(8)) Register_File (
    .Din(driver_13_out), .we(multiplexer_1_out), .Rw(Instruction_Flags), .C(Clock), .Ra(Instruction_RS0),
    .Rb(multiplexer_2_out), .Da(Register_File_da), .Db(Register_File_db));
  assign alu_1_p5 = RS1_Write_ALU_B ? Register_File_db : 8'bz;  // Driver driver_14
  assign alu_1_p6 = RS0_Write_ALU_A ? Register_File_da : 8'bz;  // Driver driver_15
  Register #(.Bits(8)) IR_0 (
    .D(driver_16_out), .C(Clock), .en(IR0_Read_Data_Bus), .Q({Instruction_Flags, Instruction_Opcode}));
  assign driver_16_out = IR0_Read_Data_Bus ? driver_3_out : 8'bz;  // Driver driver_16
  LED led_3 (.in(Instruction_Opcode[3]));
  LED led_4 (.in(Instruction_Opcode[2]));
  LED led_5 (.in(Instruction_Opcode[1]));
  LED led_6 (.in(Instruction_Opcode[0]));

  // Other names for the same wires on the sheet: Instruction_Funct[3:0] = Instruction_Flags;
  //   Instruction_RD[3:0] = Instruction_Flags; DataBus_Out[7:0] = Data_OUT

  // Notes on the sheet:
  //   clk: Hz: 3
  //   This is just a little showcase, since my CPU is WIP.
  //   Later on, I'll finally make an ALU and Jumping implemented.
  //   And now I'd like to show some work i did on memory accessing on my CPU.
  //   uCode
  //   contents of uCode_3 (hex, n*v repeats v):
  //   80,80,80,13*0,80,80,80,13*0,80,80,80,13*0,80,80,80,0,80,11*0,80,80,80
  //   ,0,40
  //   Program Counter
  //   contents of uCode_2 (hex, n*v repeats v):
  //   83*0,f
  //   contents of uCode_1 (hex, n*v repeats v):
  //   80,80,80,13*0,80,80,80,3,12*0,80,80,80,21,12*0,80,80,80,18,89
  //   ,11*0,80,80,80,18,48,11*0,80,80,80,1
  //   contents of eeprom_1 (hex, n*v repeats v):
  //   12,0,a,22,0,f,35,21,0,41,3
  //   contents of uCode_0 (hex, n*v repeats v):
  //   16,26,46,13*0,16,26,46,1,12*0,16,26,46,1,12*0,16,26,46,0,1,11*0
  //   ,16,26,46,0,81,11*0,16,26,46,1
  //   Register File
  //   Address Calculation
  //   ALU
  //   Instruction Register
  //   Status Register
endmodule
